# Fritzing sketch breadboard (saved by Fritzing 0.9.6b)
breadboards: 1

parts:
  R1 = PHOTOCELL [package=photocell-kit]
  LED1 = LED - 5mm [color="Red (633nm)" current=0.030 package="5 mm [THT]"]
  R2 = Resistor [tolerance=±5% resistance=10k package="2010 [SMD]"]  # not connected
  R3 = Resistor [tolerance=±5% resistance=220 package="2010 [SMD]"]
  HC-SR04_Sensor_1 = HC-SR04 Ultrasonic Distance Sensor
  J1 = Piezo Speaker
  R4 = Resistor [tolerance=±5% resistance=100 package="2010 [SMD]"]
  Part1 = Croduino NOVA
  YL-83_-_Control_Board1 = YL-83 Rain Sensor - Control Board
  YL-83_-_Detection_Board1 = YL-83 Rain Sensor - Detection Board
  J2 = Basic Servo

nets:
  N1: R1.P$1, Part1.A
  VCC: R1.P$2, HC-SR04_Sensor_1.VCC, Part1.5V, YL-83_-_Control_Board1.VCC, J2.vcc
  GND: LED1.cathode, HC-SR04_Sensor_1.GND, J1.pin1, Part1.GND, YL-83_-_Control_Board1.GND, J2.gnd
  N2: LED1.anode, R3.Pin_1
  N3: R3.Pin_0, Part1.#13
  N4: HC-SR04_Sensor_1.TRIG, Part1.#12
  N5: HC-SR04_Sensor_1.ECHO, Part1.#14
  N6: J1.pin2, R4.Pin_1
  N7: R4.Pin_0, Part1.#4
  N8: Part1.#16, J2.pulse
  N9: Part1.#5, YL-83_-_Control_Board1.DO
  N10: YL-83_-_Control_Board1.POS, YL-83_-_Detection_Board1.POS
  N11: YL-83_-_Control_Board1.NEG, YL-83_-_Detection_Board1.NEG

custom parts:
  YL-83 Rain Sensor - Control Board: The YL-83 is a rain sensor that has more resistance when dry and less resistance when wet. The module runs at 5V.
  YL-83 Rain Sensor - Detection Board: The YL-83 is a rain sensor that has more resistance when dry and less resistance when wet. The module runs at 5V.
